# Fritzing sketch schematic (saved by Fritzing 0.9.8b)

parts:
  Mod1 = Raspberry Pi Pico
  S1 = Square Pushbutton
  S2 = Square Pushbutton
  S3 = Square Pushbutton
  S4 = Square Pushbutton
  S5 = Square Pushbutton
  S6 = Square Pushbutton

nets:
  N1: Mod1.pin_1, S1.leg1
  N2: Mod1.pin_2, S2.leg1
  N3: Mod1.pin_4, S3.leg1
  N4: Mod1.pin_5, S4.leg1
  N5: Mod1.pin_6, S5.leg1
  N6: Mod1.pin_7, S6.leg1
  N7: Mod1.pin_8, Mod1.pin_42, S1.leg0, S2.leg0, S3.leg0, S4.leg0, S5.leg0, S6.leg0

custom parts:
  Raspberry Pi Pico: Raspberry Pi Pico. Based around the RP2040 microcontroller the Pico is a low cost microcontroller device bringing Raspberry Pi quality, cost, and easy of use to the microcontroller space. Jan 2021, Split part in to two versions: tht (this one) and SMD. This one will drill holes for a .1 in header in pcb to allow plugging in the module as well as providing pads to solder the module to the top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
